// Logisim project 32mux1.circ as structural Verilog: 1 circuit, main circuit main
module main (
  input  A,
  input  B,
  input  C,
  input  D,
  input  E,
  output Y
);

  wire and_1_out, and_2_out, and_3_out, and_4_out, decoder_1_out0, decoder_1_out1, decoder_1_out2,
       decoder_1_out3, multiplexer_1_out, multiplexer_2_out, multiplexer_3_out, multiplexer_4_out;

  Decoder #(.select(2)) decoder_1 (
    .out0(decoder_1_out0), .out1(decoder_1_out1), .out2(decoder_1_out2), .out3(decoder_1_out3), .sel({B, A}),
    .en(1'b1));
  Multiplexer #(.select(3)) multiplexer_1 (
    .in0(1'b0), .in1(1'b1), .in2(1'b1), .in3(1'b1), .in4(1'b1), .in5(1'b0), .in6(1'b0), .in7(1'b1),
    .out(multiplexer_1_out), .sel({E, D, C}));  // open: en
  Multiplexer #(.select(3)) multiplexer_2 (
    .in0(1'b1), .in1(1'b0), .in2(1'b1), .in3(1'b0), .in4(1'b0), .in5(1'b1), .in6(1'b1), .in7(1'b0),
    .out(multiplexer_2_out), .sel({E, D, C}));  // open: en
  Multiplexer #(.select(3)) multiplexer_3 (
    .in0(1'b0), .in1(1'b1), .in2(1'b0), .in3(1'b1), .in4(1'b1), .in5(1'b1), .in6(1'b0), .in7(1'b1),
    .out(multiplexer_3_out), .sel({E, D, C}));  // open: en
  Multiplexer #(.select(3)) multiplexer_4 (
    .in0(1'b1), .in1(1'b0), .in2(1'b1), .in3(1'b0), .in4(1'b1), .in5(1'b0), .in6(1'b1), .in7(1'b1),
    .out(multiplexer_4_out), .sel({E, D, C}));  // open: en
  and and_1 (and_1_out, decoder_1_out0, multiplexer_1_out);
  and and_2 (and_2_out, decoder_1_out1, multiplexer_2_out);
  and and_3 (and_3_out, decoder_1_out2, multiplexer_3_out);
  and and_4 (and_4_out, decoder_1_out3, multiplexer_4_out);
  or or_1 (Y, and_1_out, and_2_out, and_3_out, and_4_out);
endmodule
