// Logisim project mod5.circ as structural Verilog
module mod5 (
  input  In,
  output S0,
  output S1,
  output S2,
  output S3,
  output S4
);

  wire clock_1_out;
  wire [1:1] register_1_q, register_1_q_2;

  Clock clock_1 (.out(clock_1_out));
  Register #(.width(2)) register_1 (
    .D({register_1_q[1], In}), .en(1'b1), .Q({register_1_q_2[1], register_1_q[1]}), .clk(clock_1_out));  // open: clr
  Decoder #(.select(2)) decoder_1 (
    .out0(S1), .out1(S2), .out2(S4), .out3(S3), .sel({register_1_q[1], In}));  // open: en

  assign S0 = 1'b0;
endmodule
