// Logisim project paixu.circ as structural Verilog
module _1bit_swap (
  input  l1,
  input  l2,
  input  S,
  output O1,
  output O2
);

  wire not_1_out, or_1_out, or_2_out, or_3_out, or_4_out;

  not not_1 (not_1_out, S);
  or or_1 (or_1_out, l1, S);
  or or_2 (or_2_out, l2, not_1_out);
  or or_3 (or_3_out, l1, not_1_out);
  or or_4 (or_4_out, l2, S);
  and and_1 (O1, or_1_out, or_2_out);
  and and_2 (O2, or_3_out, or_4_out);
endmodule

module _4bit_swap (
  input  [3:0] l1,
  input  [3:0] l2,
  input  S,
  output [3:0] O1,
  output [3:0] O2
);

  _1bit_swap u_1bit_swap_1 (.l1(l1[0]), .l2(l2[0]), .S(S), .O1(O1[0]), .O2(O2[0]));
  _1bit_swap u_1bit_swap_2 (.l1(l1[1]), .l2(l2[1]), .S(S), .O1(O1[1]), .O2(O2[1]));
  _1bit_swap u_1bit_swap_3 (.l1(l1[2]), .l2(l2[2]), .S(S), .O1(O1[2]), .O2(O2[2]));
  _1bit_swap u_1bit_swap_4 (.l1(l1[3]), .l2(l2[3]), .S(S), .O1(O1[3]), .O2(O2[3]));
endmodule

module _4bit_sort (
  input  [3:0] A,
  input  [3:0] B,
  input  [3:0] C,
  input  [3:0] D,
  output [3:0] _1,
  output [3:0] _2,
  output [3:0] _3,
  output [3:0] _4
);

  wire comparator_1_lt, comparator_2_lt, comparator_3_lt, comparator_4_lt, comparator_5_lt, comparator_6_lt,
       not_1_out, not_2_out, not_3_out, not_4_out, not_5_out, not_6_out;
  wire [3:0] n4bit_swap_1_o1, n4bit_swap_1_o2, n4bit_swap_2_o1, n4bit_swap_2_o2, n4bit_swap_3_o1,
       n4bit_swap_3_o2, n4bit_swap_4_o2, n4bit_swap_6_o2;

  Comparator #(.width(4), .mode("unsigned")) comparator_1 (.a(A), .b(B), .lt(comparator_1_lt));  // open: gt, eq
  not not_1 (not_1_out, comparator_1_lt);
  _4bit_swap u_4bit_swap_1 (.l1(A), .l2(B), .S(not_1_out), .O1(n4bit_swap_1_o1), .O2(n4bit_swap_1_o2));
  Comparator #(.width(4), .mode("unsigned")) comparator_2 (
    .a(n4bit_swap_1_o2), .b(n4bit_swap_3_o2), .lt(comparator_2_lt));  // open: gt, eq
  not not_2 (not_2_out, comparator_2_lt);
  Comparator #(.width(4), .mode("unsigned")) comparator_3 (
    .a(n4bit_swap_1_o1), .b(C), .lt(comparator_3_lt));  // open: gt, eq
  not not_3 (not_3_out, comparator_3_lt);
  _4bit_swap u_4bit_swap_2 (
    .l1(n4bit_swap_1_o2), .l2(n4bit_swap_3_o2), .S(not_2_out), .O1(n4bit_swap_2_o1), .O2(n4bit_swap_2_o2));
  _4bit_swap u_4bit_swap_3 (.l1(n4bit_swap_1_o1), .l2(C), .S(not_3_out), .O1(n4bit_swap_3_o1), .O2(n4bit_swap_3_o2));
  Comparator #(.width(4), .mode("unsigned")) comparator_4 (
    .a(n4bit_swap_2_o1), .b(n4bit_swap_6_o2), .lt(comparator_4_lt));  // open: gt, eq
  not not_4 (not_4_out, comparator_4_lt);
  Comparator #(.width(4), .mode("unsigned")) comparator_5 (
    .a(n4bit_swap_2_o2), .b(n4bit_swap_4_o2), .lt(comparator_5_lt));  // open: gt, eq
  not not_5 (not_5_out, comparator_5_lt);
  Comparator #(.width(4), .mode("unsigned")) comparator_6 (
    .a(n4bit_swap_3_o1), .b(D), .lt(comparator_6_lt));  // open: gt, eq
  _4bit_swap u_4bit_swap_4 (.l1(n4bit_swap_2_o1), .l2(n4bit_swap_6_o2), .S(not_4_out), .O1(_2), .O2(n4bit_swap_4_o2));
  _4bit_swap u_4bit_swap_5 (.l1(n4bit_swap_2_o2), .l2(n4bit_swap_4_o2), .S(not_5_out), .O1(_3), .O2(_4));
  _4bit_swap u_4bit_swap_6 (.l1(n4bit_swap_3_o1), .l2(D), .S(not_6_out), .O1(_1), .O2(n4bit_swap_6_o2));
  not not_6 (not_6_out, comparator_6_lt);
endmodule

module mod5 (
  input  in,
  input  s1,
  input  s2,
  input  s3,
  input  s4,
  output s1_2,
  output s2_2,
  output s3_2,
  output s4_2
);

  wire not_1_out, not_2_out, not_3_out, not_4_out, not_5_out, not_6_out, not_7_out, not_8_out, not_9_out,
       not_10_out;

  not not_1 (not_1_out, in);
  not not_2 (not_2_out, s2);
  not not_3 (not_3_out, s3);
  not not_4 (not_4_out, s2);
  not not_5 (not_5_out, s3);
  not not_6 (not_6_out, s1);
  not not_7 (not_7_out, s4);
  not not_8 (not_8_out, in);
  not not_9 (not_9_out, s1);
  not not_10 (not_10_out, s4);
  and and_1 (s1_2, not_1_out, not_2_out, not_3_out);
  and and_2 (s2_2, in, not_4_out, not_5_out);
  and and_3 (s3_2, in, not_6_out, not_7_out);
  and and_4 (s4_2, not_8_out, not_9_out, not_10_out);
endmodule

module fsm (
  input  in_1,
  output out_2,
  output out_3,
  output out_4,
  output out_5,
  output out_6
);

  wire clock_1_out;
  wire [3:0] mod5_1_s1_2;

  mod5 mod5_1 (
    .in(in_1), .s1(out_3), .s2(out_4), .s3(out_5), .s4(out_6), .s1_2(mod5_1_s1_2[0]), .s2_2(mod5_1_s1_2[1]),
    .s3_2(mod5_1_s1_2[2]), .s4_2(mod5_1_s1_2[3]));
  Register #(.width(4)) register_1 (
    .D(mod5_1_s1_2), .Q({out_6, out_5, out_4, out_3}), .clk(clock_1_out));  // open: en, clr
  Clock clock_1 (.out(clock_1_out));
  Multiplexer multiplexer_1 ();  // open: in0, in1, out, sel, en

  assign out_2 = 1'b0;
endmodule
