// Logisim project 快速幂.circ as structural Verilog: 2 circuits, main circuit main
module main (
  input  [31:0] in,
  output [31:0] Output
);

  wire a1_2_q, a1_q, clock_1_out, clock_2_out, clock_3_out, clock_4_out, clock_5_out, clock_6_out,
       clock_7_out, fflag, flag, tepan;
  wire [31:0] a0, A1, a1_t, A2, a2_t, A3, a3_t, A4, adder_1_out, adder_2_out, adder_3_out, adder_4_out, b0,
       b1, b2, b3, multiplexer_1_out, multiplexer_2_out, multiplexer_3_out, multiplexer_4_out,
       multiplexer_5_out, multiplexer_6_out, multiplexer_7_out, multiplexer_8_out, multiplexer_9_out,
       multiplier_1_out, multiplier_2_out, multiplier_3_out, multiplier_4_out, multiplier_5_out,
       multiplier_6_out, multiplier_7_out, multiplier_8_out, multiplier_9_out, multiplier_10_out,
       multiplier_11_out, multiplier_12_out, multiplier_13_out, multiplier_14_out, multiplier_15_out,
       multiplier_16_out;

  Register #(.width(1)) u_a1 (.D(1'b1), .en(flag), .Q(a1_q), .clk(clock_1_out));  // open: clr
  Clock clock_1 (.out(clock_1_out));
  Multiplexer #(.width(32)) multiplexer_1 (.in0(32'h1), .in1(b0), .out(multiplexer_1_out), .sel(a1_q));  // open: en
  Multiplexer #(.width(32)) multiplexer_2 (
    .in0({32{1'b0}}), .in1(b1), .out(multiplexer_2_out), .sel(a1_q));  // open: en
  Multiplexer #(.width(32)) multiplexer_3 (
    .in0({32{1'b0}}), .in1(b2), .out(multiplexer_3_out), .sel(a1_q));  // open: en
  Multiplexer #(.width(32)) multiplexer_4 (.in0(32'h1), .in1(b3), .out(multiplexer_4_out), .sel(a1_q));  // open: en
  in in_1 (.in(in), .tepan(tepan), .fflag(fflag), .flag(flag));
  Multiplier #(.width(32)) multiplier_1 (.a(A1), .b(multiplexer_1_out), .out(multiplier_1_out));  // open: cin, cout
  Multiplier #(.width(32)) multiplier_2 (.a(A2), .b(multiplexer_3_out), .out(multiplier_2_out));  // open: cin, cout
  Multiplier #(.width(32)) multiplier_3 (.a(A1), .b(multiplexer_2_out), .out(multiplier_3_out));  // open: cin, cout
  Multiplier #(.width(32)) multiplier_4 (.a(A2), .b(multiplexer_4_out), .out(multiplier_4_out));  // open: cin, cout
  Multiplier #(.width(32)) multiplier_5 (.a(A3), .b(multiplexer_1_out), .out(multiplier_5_out));  // open: cin, cout
  Multiplier #(.width(32)) multiplier_6 (.a(A4), .b(multiplexer_3_out), .out(multiplier_6_out));  // open: cin, cout
  Multiplier #(.width(32)) multiplier_7 (.a(A3), .b(multiplexer_2_out), .out(multiplier_7_out));  // open: cin, cout
  Multiplier #(.width(32)) multiplier_8 (.a(A4), .b(multiplexer_4_out), .out(multiplier_8_out));  // open: cin, cout
  Adder #(.width(32)) adder_1 (.a(multiplier_1_out), .b(multiplier_2_out), .out(adder_1_out));  // open: cin, cout
  Adder #(.width(32)) adder_2 (.a(multiplier_3_out), .b(multiplier_4_out), .out(adder_2_out));  // open: cin, cout
  Adder #(.width(32)) adder_3 (.a(multiplier_5_out), .b(multiplier_6_out), .out(adder_3_out));  // open: cin, cout
  Adder #(.width(32)) adder_4 (.a(multiplier_8_out), .b(multiplier_7_out), .out(adder_4_out));  // open: cin, cout
  Register #(.width(1)) a1_2 (.D(1'b1), .en(fflag), .Q(a1_2_q), .clk(clock_2_out));  // open: clr
  Clock clock_2 (.out(clock_2_out));
  Multiplexer #(.width(32)) multiplexer_5 (.in0(32'h1), .in1(a0), .out(multiplexer_5_out), .sel(a1_2_q));  // open: en
  Multiplexer #(.width(32)) multiplexer_6 (.in0(32'h1), .in1(a1_t), .out(multiplexer_6_out), .sel(a1_2_q));  // open: en
  Multiplexer #(.width(32)) multiplexer_7 (.in0(32'h1), .in1(a2_t), .out(multiplexer_7_out), .sel(a1_2_q));  // open: en
  Multiplexer #(.width(32)) multiplexer_8 (
    .in0({32{1'b0}}), .in1(a3_t), .out(multiplexer_8_out), .sel(a1_2_q));  // open: en
  Clock clock_3 (.out(clock_3_out));
  Clock clock_4 (.out(clock_4_out));
  Clock clock_5 (.out(clock_5_out));
  Clock clock_6 (.out(clock_6_out));
  Clock clock_7 (.out(clock_7_out));
  Register #(.width(32)) register_1 (.D(adder_1_out), .en(flag), .Q(b0), .clk(clock_4_out));  // open: clr
  Register #(.width(32)) register_2 (.D(adder_2_out), .en(flag), .Q(b1), .clk(clock_5_out));  // open: clr
  Register #(.width(32)) register_3 (.D(adder_3_out), .en(flag), .Q(b2), .clk(clock_6_out));  // open: clr
  Register #(.width(32)) register_4 (.D(adder_4_out), .en(flag), .Q(b3), .clk(clock_7_out));  // open: clr
  Register #(.width(32)) u_a0 (.D(multiplexer_5_out), .en(fflag), .Q(A1), .clk(clock_3_out));  // open: clr
  Register #(.width(32)) a1_3 (.D(multiplexer_6_out), .en(fflag), .Q(A2), .clk(clock_3_out));  // open: clr
  Register #(.width(32)) u_a2 (.D(multiplexer_7_out), .en(fflag), .Q(A3), .clk(clock_3_out));  // open: clr
  Register #(.width(32)) u_a3 (.D(multiplexer_8_out), .en(fflag), .Q(A4), .clk(clock_3_out));  // open: clr
  Multiplexer #(.width(32)) multiplexer_9 (
    .in0(adder_1_out), .in1(32'h1), .out(multiplexer_9_out), .sel(tepan));  // open: en
  Multiplexer #(.width(32)) multiplexer_10 (
    .in0(multiplexer_9_out), .in1({32{1'b0}}), .out(Output), .sel(fflag));  // open: en
  Multiplier #(.width(32)) multiplier_9 (.a(A1), .b(A1), .out(multiplier_9_out));  // open: cin, cout
  Multiplier #(.width(32)) multiplier_10 (.a(A1), .b(A2), .out(multiplier_10_out));  // open: cin, cout
  Multiplier #(.width(32)) multiplier_11 (.a(A2), .b(A4), .out(multiplier_11_out));  // open: cin, cout
  Multiplier #(.width(32)) multiplier_12 (.a(A2), .b(A3), .out(multiplier_12_out));  // open: cin, cout
  Multiplier #(.width(32)) multiplier_13 (.a(A3), .b(A1), .out(multiplier_13_out));  // open: cin, cout
  Multiplier #(.width(32)) multiplier_14 (.a(A3), .b(A4), .out(multiplier_14_out));  // open: cin, cout
  Multiplier #(.width(32)) multiplier_15 (.a(A4), .b(A4), .out(multiplier_15_out));  // open: cin, cout
  Multiplier #(.width(32)) multiplier_16 (.a(A2), .b(A3), .out(multiplier_16_out));  // open: cin, cout
  Adder #(.width(32)) adder_5 (.a(multiplier_9_out), .b(multiplier_12_out), .out(a0));  // open: cin, cout
  Adder #(.width(32)) adder_6 (.a(multiplier_10_out), .b(multiplier_11_out), .out(a1_t));  // open: cin, cout
  Adder #(.width(32)) adder_7 (.a(multiplier_13_out), .b(multiplier_14_out), .out(a2_t));  // open: cin, cout
  Adder #(.width(32)) adder_8 (.a(multiplier_16_out), .b(multiplier_15_out), .out(a3_t));  // open: cin, cout
endmodule

module in (
  input  [31:0] in,
  output tepan,
  output fflag,
  output flag
);

  wire clock_1_out, clock_2_out, comparator_1_eq, comparator_3_lt, not_1_out, register_1_q;
  wire [31:0] divider_1_out, divider_1_rem, multiplexer_1_out, multiplexer_2_out, register_2_q,
       subtractor_1_out;

  Comparator #(.width(32)) comparator_1 (.a(in), .b({32{1'b0}}), .eq(comparator_1_eq));  // open: gt, lt
  Comparator #(.width(32)) comparator_2 (.a(in), .b(32'h1), .eq(tepan));  // open: gt, lt
  Subtractor #(.width(32)) subtractor_1 (.a(in), .b(32'h1), .out(subtractor_1_out));  // open: bin, bout
  not not_1 (not_1_out, comparator_1_eq);
  Multiplexer #(.width(32)) multiplexer_1 (
    .in0({32{1'b0}}), .in1(subtractor_1_out), .out(multiplexer_1_out), .sel(not_1_out));  // open: en
  Register #(.width(1)) register_1 (.D(1'b1), .en(1'b1), .Q(register_1_q), .clk(clock_1_out));  // open: clr
  Clock clock_1 (.out(clock_1_out));
  Multiplexer #(.width(32)) multiplexer_2 (
    .in0(multiplexer_1_out), .in1(divider_1_out), .out(multiplexer_2_out), .sel(register_1_q));  // open: en
  Register #(.width(32)) register_2 (
    .D(multiplexer_2_out), .en(1'b1), .Q(register_2_q), .clk(clock_2_out));  // open: clr
  Clock clock_2 (.out(clock_2_out));
  Divider #(.width(32)) divider_1 (
    .a(register_2_q), .b(32'h2), .out(divider_1_out), .rem(divider_1_rem));  // open: upper
  Comparator #(.width(32), .mode("unsigned")) comparator_3 (
    .a(multiplexer_2_out), .b(32'h1), .lt(comparator_3_lt));  // open: gt, eq
  not not_2 (fflag, comparator_3_lt);
  and and_1 (flag, fflag, divider_1_rem[0]);
endmodule
