// Logisim project 课下3GRF.circ as structural Verilog: 1 circuit, main circuit grf
module grf (
  input  clk,
  input  reset,
  input  WE,
  input  [4:0] A1,
  input  [4:0] A2,
  input  [4:0] A3,
  input  [31:0] WD,
  output [31:0] RD1,
  output [31:0] RD2
);

  wire and_1_out, and_2_out, and_3_out, and_4_out, and_5_out, and_6_out, and_7_out, and_8_out, and_9_out,
       and_10_out, and_11_out, and_12_out, and_13_out, and_14_out, and_15_out, and_16_out, and_17_out,
       and_18_out, and_19_out, and_20_out, and_21_out, and_22_out, and_23_out, and_24_out, and_25_out,
       and_26_out, and_27_out, and_28_out, and_29_out, and_30_out, and_31_out, and_32_out, En0, En1, En2,
       En3, En4, En5, En6, En7, En8, En9, En10, En11, En12, En13, En14, En15, En16, En17, En18, En19, En20,
       En21, En22, En23, En24, En25, En26, En27, En28, En29, En30, En31;
  wire [31:0] out0, out1, out2, out3, out4, out5, out6, out7, out8, out9, out10, out11, out12, out13, out14,
       out15, out16, out17, out18, out19, out20, out21, out22, out23, out24, out25, out26, out27, out28,
       out29, out30, out31;

  Demultiplexer #(.select(5), .enable("false")) demultiplexer_1 (
    .out0(En0), .out1(En1), .out2(En2), .out3(En3), .out4(En4), .out5(En5), .out6(En6), .out7(En7),
    .out8(En8), .out9(En9), .out10(En10), .out11(En11), .out12(En12), .out13(En13), .out14(En14),
    .out15(En15), .out16(En16), .out17(En17), .out18(En18), .out19(En19), .out20(En20), .out21(En21),
    .out22(En22), .out23(En23), .out24(En24), .out25(En25), .out26(En26), .out27(En27), .out28(En28),
    .out29(En29), .out30(En30), .out31(En31), .in(1'b1), .sel(A3));
  Multiplexer #(.select(5), .width(32)) multiplexer_1 (
    .in0(out0), .in1(out1), .in2(out2), .in3(out3), .in4(out4), .in5(out5), .in6(out6), .in7(out7),
    .in8(out8), .in9(out9), .in10(out10), .in11(out11), .in12(out12), .in13(out13), .in14(out14),
    .in15(out15), .in16(out16), .in17(out17), .in18(out18), .in19(out19), .in20(out20), .in21(out21),
    .in22(out22), .in23(out23), .in24(out24), .in25(out25), .in26(out26), .in27(out27), .in28(out28),
    .in29(out29), .in30(out30), .in31(out31), .out(RD2), .sel(A2), .en(1'b1));
  Multiplexer #(.select(5), .width(32)) multiplexer_2 (
    .in0(out0), .in1(out1), .in2(out2), .in3(out3), .in4(out4), .in5(out5), .in6(out6), .in7(out7),
    .in8(out8), .in9(out9), .in10(out10), .in11(out11), .in12(out12), .in13(out13), .in14(out14),
    .in15(out15), .in16(out16), .in17(out17), .in18(out18), .in19(out19), .in20(out20), .in21(out21),
    .in22(out22), .in23(out23), .in24(out24), .in25(out25), .in26(out26), .in27(out27), .in28(out28),
    .in29(out29), .in30(out30), .in31(out31), .out(RD1), .sel(A1), .en(1'b1));
  Register #(.width(32)) register_1 (.D({32{1'b0}}), .en(and_1_out), .Q(out0), .clk(clk), .clr(reset));
  and and_1 (and_1_out, En0, WE);
  Register #(.width(32)) register_2 (.D(WD), .en(and_2_out), .Q(out1), .clk(clk), .clr(reset));
  and and_2 (and_2_out, En1, WE);
  Register #(.width(32)) register_3 (.D(WD), .en(and_3_out), .Q(out5), .clk(clk), .clr(reset));
  and and_3 (and_3_out, En5, WE);
  Register #(.width(32)) register_4 (.D(WD), .en(and_4_out), .Q(out9), .clk(clk), .clr(reset));
  and and_4 (and_4_out, En9, WE);
  Register #(.width(32)) register_5 (.D(WD), .en(and_5_out), .Q(out13), .clk(clk), .clr(reset));
  and and_5 (and_5_out, En13, WE);
  Register #(.width(32)) register_6 (.D(WD), .en(and_6_out), .Q(out17), .clk(clk), .clr(reset));
  and and_6 (and_6_out, En17, WE);
  Register #(.width(32)) register_7 (.D(WD), .en(and_7_out), .Q(out21), .clk(clk), .clr(reset));
  and and_7 (and_7_out, En21, WE);
  Register #(.width(32)) register_8 (.D(WD), .en(and_8_out), .Q(out25), .clk(clk), .clr(reset));
  and and_8 (and_8_out, En25, WE);
  and and_9 (and_9_out, En29, WE);
  Register #(.width(32)) register_9 (.D(WD), .en(and_9_out), .Q(out29), .clk(clk), .clr(reset));
  and and_10 (and_10_out, En2, WE);
  and and_11 (and_11_out, En6, WE);
  and and_12 (and_12_out, En10, WE);
  and and_13 (and_13_out, En14, WE);
  and and_14 (and_14_out, En18, WE);
  and and_15 (and_15_out, En22, WE);
  and and_16 (and_16_out, En26, WE);
  Register #(.width(32)) register_10 (.D(WD), .en(and_10_out), .Q(out2), .clk(clk), .clr(reset));
  Register #(.width(32)) register_11 (.D(WD), .en(and_11_out), .Q(out6), .clk(clk), .clr(reset));
  Register #(.width(32)) register_12 (.D(WD), .en(and_12_out), .Q(out10), .clk(clk), .clr(reset));
  Register #(.width(32)) register_13 (.D(WD), .en(and_13_out), .Q(out14), .clk(clk), .clr(reset));
  Register #(.width(32)) register_14 (.D(WD), .en(and_14_out), .Q(out18), .clk(clk), .clr(reset));
  Register #(.width(32)) register_15 (.D(WD), .en(and_15_out), .Q(out22), .clk(clk), .clr(reset));
  Register #(.width(32)) register_16 (.D(WD), .en(and_16_out), .Q(out26), .clk(clk), .clr(reset));
  Register #(.width(32)) register_17 (.D(WD), .en(and_17_out), .Q(out30), .clk(clk), .clr(reset));
  and and_17 (and_17_out, En30, WE);
  Register #(.width(32)) register_18 (.D(WD), .en(and_18_out), .Q(out3), .clk(clk), .clr(reset));
  and and_18 (and_18_out, En3, WE);
  Register #(.width(32)) register_19 (.D(WD), .en(and_19_out), .Q(out7), .clk(clk), .clr(reset));
  and and_19 (and_19_out, En7, WE);
  Register #(.width(32)) register_20 (.D(WD), .en(and_20_out), .Q(out11), .clk(clk), .clr(reset));
  and and_20 (and_20_out, En11, WE);
  Register #(.width(32)) register_21 (.D(WD), .en(and_21_out), .Q(out15), .clk(clk), .clr(reset));
  and and_21 (and_21_out, En15, WE);
  Register #(.width(32)) register_22 (.D(WD), .en(and_22_out), .Q(out19), .clk(clk), .clr(reset));
  and and_22 (and_22_out, En19, WE);
  Register #(.width(32)) register_23 (.D(WD), .en(and_23_out), .Q(out23), .clk(clk), .clr(reset));
  and and_23 (and_23_out, En23, WE);
  Register #(.width(32)) register_24 (.D(WD), .en(and_24_out), .Q(out27), .clk(clk), .clr(reset));
  and and_24 (and_24_out, En27, WE);
  and and_25 (and_25_out, En31, WE);
  Register #(.width(32)) register_25 (.D(WD), .en(and_25_out), .Q(out31), .clk(clk), .clr(reset));
  and and_26 (and_26_out, En4, WE);
  and and_27 (and_27_out, En8, WE);
  and and_28 (and_28_out, En12, WE);
  and and_29 (and_29_out, En16, WE);
  and and_30 (and_30_out, En20, WE);
  and and_31 (and_31_out, En24, WE);
  and and_32 (and_32_out, En28, WE);
  Register #(.width(32)) register_26 (.D(WD), .en(and_26_out), .Q(out4), .clk(clk), .clr(reset));
  Register #(.width(32)) register_27 (.D(WD), .en(and_27_out), .Q(out8), .clk(clk), .clr(reset));
  Register #(.width(32)) register_28 (.D(WD), .en(and_28_out), .Q(out12), .clk(clk), .clr(reset));
  Register #(.width(32)) register_29 (.D(WD), .en(and_29_out), .Q(out16), .clk(clk), .clr(reset));
  Register #(.width(32)) register_30 (.D(WD), .en(and_30_out), .Q(out20), .clk(clk), .clr(reset));
  Register #(.width(32)) register_31 (.D(WD), .en(and_31_out), .Q(out24), .clk(clk), .clr(reset));
  Register #(.width(32)) register_32 (.D(WD), .en(and_32_out), .Q(out28), .clk(clk), .clr(reset));

  // Other names for the same wires on the sheet: RE = reset; WR = WE
endmodule
