// Logisim project 课下4fsm.circ as structural Verilog
module circule (
  input  [1:0] now,
  input  [1:0] in,
  output out,
  output [1:0] next
);

  wire and_2_out, and_3_out, and_4_out, and_5_out, not_1_out, not_2_out, not_3_out, not_4_out, not_5_out,
       not_6_out, not_7_out;

  and and_1 (out, now[1], now[0]);
  not not_1 (not_1_out, now[1]);
  not not_2 (not_2_out, in[0]);
  not not_3 (not_3_out, now[0]);
  not not_4 (not_4_out, in[0]);
  not not_5 (not_5_out, in[1]);
  not not_6 (not_6_out, now[0]);
  not not_7 (not_7_out, in[0]);
  and and_2 (and_2_out, not_1_out, now[0], not_2_out);
  and and_3 (and_3_out, now[1], not_3_out, not_4_out);
  and and_4 (and_4_out, not_5_out, in[0]);
  and and_5 (and_5_out, now[1], not_6_out, not_7_out);
  or or_1 (next[1], and_2_out, and_3_out);
  or or_2 (next[0], and_4_out, and_5_out);
endmodule

module fsm (
  input  CLR,
  input  [1:0] In,
  output C
);

  wire circule_1_out, clock_1_out, multiplexer_1_out, not_2_out;
  wire [1:0] and_1_out, circule_1_next, not_1_out, register_1_q;

  assign not_1_out = ~{2{CLR}};  // NOT_Gate not_1, 2 bits wide
  circule circule_1 (.now(register_1_q), .in(In), .out(circule_1_out), .next(circule_1_next));
  // Probe on circule_1_next
  assign and_1_out = not_1_out & circule_1_next;  // AND_Gate and_1, 2 bits wide
  Register #(.width(2)) register_1 (.D(and_1_out), .Q(register_1_q), .clk(clock_1_out));  // open: en, clr
  Clock clock_1 (.out(clock_1_out));
  // AND_Gate and_2 has open pins: in0=CLR, in4=clock_1_out, out=open
  // Probe on register_1_q
  Multiplexer #(.select(2)) multiplexer_1 (
    .in0(1'b0), .in1(1'b0), .in2(1'b1), .in3(1'b0), .out(multiplexer_1_out), .sel(register_1_q));  // open: en
  not not_2 (not_2_out, In[0]);
  and and_3 (C, multiplexer_1_out, not_2_out);
endmodule
