// Logisim project cpu_test.circ as structural Verilog: 12 circuits, main circuit main
module main (
  input  reset,
  output [31:0] out_2,
  output out_3,
  output [4:0] out_4,
  output [31:0] out_5,
  output out_6,
  output [4:0] out_7,
  output [31:0] out_8
);

  wire ALUSrc, branch, clk, ExtOp, MemRead, RegDst, temp, zero;
  wire [1:0] MemtoReg;
  wire [2:0] ALUCtr, ALUOp;
  wire [4:0] multiplexer_2_out;
  wire [31:0] alu, dm_1_outdata, ext, grf_1_rd1, imm, multiplexer_3_out;

  Clock clock_1 (.out(clk));
  IFU ifu_1 (
    .clk(clk), .resset(reset), .in_4(imm),
    .in_5({out_2[5:0], out_2[10:6], out_2[15:11], out_2[20:16], out_2[25:21], 2'b00}), .zero(zero),
    .branch(branch), .in_2(temp), .instr(out_2));  // open: pc4
  Control control_1 (
    .Op(out_2[31:26]), .RegDst(RegDst), .branch(branch), .MemtoReg(MemtoReg), .MemRead(MemRead),
    .MemWrite(out_6), .ALUOp(ALUOp), .ALUSrc(ALUSrc), .RegWrite(out_3), .ExtOp(ExtOp), .temp(temp));
  Multiplexer #(.width(5)) multiplexer_1 (
    .in0(out_2[20:16]), .in1(out_2[15:11]), .out(out_4), .sel(RegDst));  // open: en
  Multiplexer #(.width(5)) multiplexer_2 (
    .in0(out_4), .in1({5{1'b1}}), .out(multiplexer_2_out), .sel(temp));  // open: en
  EXT ext_1 (.in_1(out_2[15:0]), .EXTOp(ExtOp), .out_3(ext));
  // Probe on ALUOp
  shift shift_1 (.In(ext), .out(imm));
  GRF grf_1 (
    .A1(out_2[25:21]), .A2(out_2[20:16]), .A3(multiplexer_2_out), .WD(out_5), .clk(clk), .reset(reset),
    .WE(out_3), .RD1(grf_1_rd1), .RD2(out_8));
  ALUControl ALUControl (.Func(out_2[5:0]), .ALUOp(ALUOp), .ALUOperation(ALUCtr));
  // Probe on ALUCtr
  Multiplexer #(.width(32)) multiplexer_3 (.in0(out_8), .in1(ext), .out(multiplexer_3_out), .sel(ALUSrc));  // open: en
  ALU alu_1 (.A(grf_1_rd1), .B(multiplexer_3_out), .ALUop(ALUCtr), .Result({alu[31:7], out_7, alu[1:0]}), .zero(zero));
  DM dm_1 (
    .MemAddr(out_7), .MemData(out_8), .MemWrite(out_6), .CLK(clk), .MemRead(MemRead), .reset(reset),
    .OutData(dm_1_outdata));
  Multiplexer #(.select(2), .width(32)) multiplexer_4 (
    .in0({alu[31:7], out_7, alu[1:0]}), .in1(dm_1_outdata), .in2({out_2[15:0], {16{1'b0}}}), .out(out_5),
    .sel(MemtoReg));  // open: in3, en
  // Probe on MemtoReg

  // Other names for the same wires on the sheet: _28[27:2] = {out_2[5:0], out_2[10:6], out_2[15:11], out_2[20:16], out_2[25:21]};
  //   instr[31:0] = out_2; alu[6:2] = out_7; MemAdder[4:0] = out_7; lui[31:16] = out_2[15:0]; MemData[31:0] = out_8;
  //   MemWrite = out_6; re = reset; RegAdder[4:0] = out_4; RegWrite = out_3; WD[31:0] = out_5
endmodule

module GRF (
  input  clk,
  input  reset,
  input  WE,
  input  [4:0] A1,
  input  [4:0] A2,
  input  [4:0] A3,
  input  [31:0] WD,
  output [31:0] RD1,
  output [31:0] RD2
);

  wire [31:0] demultiplexer_1_out0, En1, En2, En3, En4, En5, En6, En7, En8, En9, En10, En11, En12, En13,
       En14, En15, En16, En17, En18, En19, En20, En21, En22, En23, En24, En25, En26, En27, En28, En29, En30,
       En31, out1, out2, out3, out4, out5, out6, out7, out8, out9, out10, out11, out12, out13, out14, out15,
       out16, out17, out18, out19, out20, out21, out22, out23, out24, out25, out26, out27, out28, out29,
       out30, out31;

  Demultiplexer #(.select(5), .width(32), .tristate("true"), .enable("false")) demultiplexer_1 (
    .out0(demultiplexer_1_out0), .out1(En1), .out2(En2), .out3(En3), .out4(En4), .out5(En5), .out6(En6),
    .out7(En7), .out8(En8), .out9(En9), .out10(En10), .out11(En11), .out12(En12), .out13(En13), .out14(En14),
    .out15(En15), .out16(En16), .out17(En17), .out18(En18), .out19(En19), .out20(En20), .out21(En21),
    .out22(En22), .out23(En23), .out24(En24), .out25(En25), .out26(En26), .out27(En27), .out28(En28),
    .out29(En29), .out30(En30), .out31(En31), .in(WD), .sel(A3));
  Multiplexer #(.select(5), .width(32)) multiplexer_1 (
    .in0({32{1'b0}}), .in1(out1), .in2(out2), .in3(out3), .in4(out4), .in5(out5), .in6(out6), .in7(out7),
    .in8(out8), .in9(out9), .in10(out10), .in11(out11), .in12(out12), .in13(out13), .in14(out14),
    .in15(out15), .in16(out16), .in17(out17), .in18(out18), .in19(out19), .in20(out20), .in21(out21),
    .in22(out22), .in23(out23), .in24(out24), .in25(out25), .in26(out26), .in27(out27), .in28(out28),
    .in29(out29), .in30(out30), .in31(out31), .out(RD2), .sel(A2), .en(1'b1));
  Multiplexer #(.select(5), .width(32)) multiplexer_2 (
    .in0({32{1'b0}}), .in1(out1), .in2(out2), .in3(out3), .in4(out4), .in5(out5), .in6(out6), .in7(out7),
    .in8(out8), .in9(out9), .in10(out10), .in11(out11), .in12(out12), .in13(out13), .in14(out14),
    .in15(out15), .in16(out16), .in17(out17), .in18(out18), .in19(out19), .in20(out20), .in21(out21),
    .in22(out22), .in23(out23), .in24(out24), .in25(out25), .in26(out26), .in27(out27), .in28(out28),
    .in29(out29), .in30(out30), .in31(out31), .out(RD1), .sel(A1), .en(1'b1));
  Register #(.width(32)) register_1 (.D(En1), .en(WE), .Q(out1), .clk(clk), .clr(reset));
  Register #(.width(32)) register_2 (.D(En5), .en(WE), .Q(out5), .clk(clk), .clr(reset));
  Register #(.width(32)) register_3 (.D(En9), .en(WE), .Q(out9), .clk(clk), .clr(reset));
  Register #(.width(32)) register_4 (.D(En13), .en(WE), .Q(out13), .clk(clk), .clr(reset));
  Register #(.width(32)) register_5 (.D(En17), .en(WE), .Q(out17), .clk(clk), .clr(reset));
  Register #(.width(32)) register_6 (.D(En21), .en(WE), .Q(out21), .clk(clk), .clr(reset));
  Register #(.width(32)) register_7 (.D(En25), .en(WE), .Q(out25), .clk(clk), .clr(reset));
  Register #(.width(32)) register_8 (.D(En29), .en(WE), .Q(out29), .clk(clk), .clr(reset));
  Register #(.width(32)) register_9 (.D(En2), .en(WE), .Q(out2), .clk(clk), .clr(reset));
  Register #(.width(32)) register_10 (.D(En6), .en(WE), .Q(out6), .clk(clk), .clr(reset));
  Register #(.width(32)) register_11 (.D(En10), .en(WE), .Q(out10), .clk(clk), .clr(reset));
  Register #(.width(32)) register_12 (.D(En18), .en(WE), .Q(out18), .clk(clk), .clr(reset));
  Register #(.width(32)) register_13 (.D(En14), .en(WE), .Q(out14), .clk(clk), .clr(reset));
  Register #(.width(32)) register_14 (.D(En22), .en(WE), .Q(out22), .clk(clk), .clr(reset));
  Register #(.width(32)) register_15 (.D(En26), .en(WE), .Q(out26), .clk(clk), .clr(reset));
  Register #(.width(32)) register_16 (.D(En30), .en(WE), .Q(out30), .clk(clk), .clr(reset));
  Register #(.width(32)) register_17 (.D(En3), .en(WE), .Q(out3), .clk(clk), .clr(reset));
  Register #(.width(32)) register_18 (.D(En7), .en(WE), .Q(out7), .clk(clk), .clr(reset));
  Register #(.width(32)) register_19 (.D(En11), .en(WE), .Q(out11), .clk(clk), .clr(reset));
  Register #(.width(32)) register_20 (.D(En15), .en(WE), .Q(out15), .clk(clk), .clr(reset));
  Register #(.width(32)) register_21 (.D(En19), .en(WE), .Q(out19), .clk(clk), .clr(reset));
  Register #(.width(32)) register_22 (.D(En23), .en(WE), .Q(out23), .clk(clk), .clr(reset));
  Register #(.width(32)) register_23 (.D(En27), .en(WE), .Q(out27), .clk(clk), .clr(reset));
  Register #(.width(32)) register_24 (.D(En31), .en(WE), .Q(out31), .clk(clk), .clr(reset));
  Register #(.width(32)) register_25 (.D(En4), .en(WE), .Q(out4), .clk(clk), .clr(reset));
  Register #(.width(32)) register_26 (.D(En8), .en(WE), .Q(out8), .clk(clk), .clr(reset));
  Register #(.width(32)) register_27 (.D(En12), .en(WE), .Q(out12), .clk(clk), .clr(reset));
  Register #(.width(32)) register_28 (.D(En20), .en(WE), .Q(out20), .clk(clk), .clr(reset));
  Register #(.width(32)) register_29 (.D(En16), .en(WE), .Q(out16), .clk(clk), .clr(reset));
  Register #(.width(32)) register_30 (.D(En24), .en(WE), .Q(out24), .clk(clk), .clr(reset));
  Register #(.width(32)) register_31 (.D(En28), .en(WE), .Q(out28), .clk(clk), .clr(reset));

  // Other names for the same wires on the sheet: RE = reset; WR = WE
endmodule

module IM (
  input  [4:0] A,
  output [31:0] Instr
);

  ROM #(.addrWidth(5), .dataWidth(32)) rom_1 (.addr(A), .data(Instr));  // open: sel

  // Notes on the sheet:
  //   contents of rom_1 (hex, n*v repeats v):
  //   3c03000a c000000
endmodule

module ALU (
  input  [31:0] A,
  input  [31:0] B,
  input  [2:0] ALUop,
  output [31:0] Result,
  output zero
);

  wire or_2_out;
  wire [0:0] comparator_1_lt;
  wire [31:0] adder_1_out, and_1_out, or_1_out, subtractor_1_out;

  Adder #(.width(32)) adder_1 (.a(A), .b(B), .out(adder_1_out));  // open: cin, cout
  Subtractor #(.width(32)) subtractor_1 (.a(A), .b(B), .out(subtractor_1_out));  // open: bin, bout
  assign and_1_out = A & B;  // AND_Gate and_1, 32 bits wide
  assign or_1_out = A | B;  // OR_Gate or_1, 32 bits wide
  Comparator #(.width(32)) comparator_1 (.a(A), .b(B), .lt(comparator_1_lt[0]));  // open: gt, eq
  Multiplexer #(.select(3), .width(32)) multiplexer_1 (
    .in0(adder_1_out), .in1(subtractor_1_out), .in2(and_1_out), .in3(or_1_out),
    .in4({{31{1'b0}}, comparator_1_lt[0]}), .in5({32{1'b0}}), .in6({32{1'b0}}), .in7({32{1'b0}}),
    .out(Result), .sel(ALUop));  // open: en
  // Probe on ALUop
  or or_2 (or_2_out, subtractor_1_out[0], subtractor_1_out[1], subtractor_1_out[2], subtractor_1_out[3], subtractor_1_out[4], subtractor_1_out[5], subtractor_1_out[6], subtractor_1_out[7], subtractor_1_out[8], subtractor_1_out[9], subtractor_1_out[10], subtractor_1_out[11], subtractor_1_out[12], subtractor_1_out[13], subtractor_1_out[14], subtractor_1_out[15], subtractor_1_out[17], subtractor_1_out[18], subtractor_1_out[19], subtractor_1_out[20], subtractor_1_out[21], subtractor_1_out[22], subtractor_1_out[23], subtractor_1_out[24], subtractor_1_out[25], subtractor_1_out[26], subtractor_1_out[27], subtractor_1_out[28], subtractor_1_out[29], subtractor_1_out[30], subtractor_1_out[31]);
  not not_1 (zero, or_2_out);
endmodule

module EXT (
  input  [15:0] in_1,
  input  EXTOp,
  output [31:0] out_3
);

  wire [31:0] bit_extender_1_out, bit_extender_2_out;

  assign bit_extender_1_out = {{16{in_1[15]}}, in_1};  // Bit_Extender bit_extender_1
  assign bit_extender_2_out = {{16{1'b0}}, in_1};  // Bit_Extender bit_extender_2
  Multiplexer #(.width(32)) multiplexer_1 (
    .in0(bit_extender_1_out), .in1(bit_extender_2_out), .out(out_3), .sel(EXTOp));  // open: en
endmodule

module DM (
  input  [4:0] MemAddr,
  input  [31:0] MemData,
  input  MemWrite,
  input  CLK,
  input  reset,
  input  MemRead,
  output [31:0] OutData
);

  RAM #(.addrWidth(5), .dataWidth(32), .bus("separate")) ram_1 (
    .addr(MemAddr), .din(MemData), .data(OutData), .str(MemWrite), .clk(CLK), .ld(MemRead), .clr(reset));  // open: sel
endmodule

module NPC (
  input  [31:0] pc,
  input  [31:0] imm,
  input  zero,
  input  branch,
  output [31:0] pc4,
  output [31:0] npc
);

  wire and_1_out;
  wire [31:0] adder_2_out;

  Adder #(.width(32)) adder_1 (.a(pc), .b(32'h4), .out(pc4));  // open: cin, cout
  Adder #(.width(32)) adder_2 (.a(pc4), .b(imm), .out(adder_2_out));  // open: cin, cout
  and and_1 (and_1_out, zero, branch);
  Multiplexer #(.width(32)) multiplexer_1 (.in0(pc4), .in1(adder_2_out), .out(npc), .sel(and_1_out));  // open: en
endmodule

module shift (
  input  [31:0] In,
  output [31:0] out
);

  Shifter #(.width(32)) shifter_1 (.in(In), .\dist (5'b00010), .out(out));
endmodule

// ALUC
module ALUControl (
  input  [5:0] Func,
  input  [2:0] ALUOp,
  output [2:0] ALUOperation
);

  wire addu_out, beq_out, lui_out, lw_out, not_1_out, not_2_out, not_3_out, not_4_out, not_5_out, not_6_out,
       not_7_out, not_8_out, not_9_out, Ori_out, subu_out, SW_out;

  not not_1 (not_1_out, ALUOp[1]);
  not not_2 (not_2_out, ALUOp[2]);
  not not_3 (not_3_out, ALUOp[0]);
  not not_4 (not_4_out, Func[4]);
  not not_5 (not_5_out, Func[5]);
  not not_6 (not_6_out, Func[3]);
  not not_7 (not_7_out, Func[2]);
  not not_8 (not_8_out, Func[0]);
  not not_9 (not_9_out, Func[1]);
  and SW (SW_out, not_2_out, not_1_out, ALUOp[0]);
  and lw (lw_out, not_2_out, not_1_out, ALUOp[0]);
  and addu (addu_out, Func[0], not_9_out, not_3_out, not_1_out, not_2_out, not_7_out, not_6_out, not_4_out, Func[5]);
  and subu (subu_out, not_1_out, not_2_out, not_3_out, Func[5], not_4_out, not_6_out, not_7_out, Func[1], Func[0]);
  and Ori (Ori_out, not_2_out, ALUOp[1], ALUOp[0]);
  and lui (lui_out, ALUOp[2], ALUOp[1], ALUOp[0]);
  and beq (beq_out, not_2_out, ALUOp[1], not_3_out);
  buf _2 (ALUOperation[2], lui_out);  // OR_Gate
  or _1 (ALUOperation[1], Ori_out, lui_out);
  or _0 (ALUOperation[0], lui_out, beq_out, subu_out, Ori_out);
endmodule

module Control (
  input  [5:0] Op,
  output RegDst,
  output branch,
  output [1:0] MemtoReg,
  output MemRead,
  output MemWrite,
  output [2:0] ALUOp,
  output ALUSrc,
  output RegWrite,
  output ExtOp,
  output temp
);

  wire addu_out, beq_out, lui_out, lw_out, not_1_out, not_2_out, not_3_out, not_4_out, not_5_out, not_6_out,
       subu_out, sw_out;

  not not_1 (not_1_out, Op[3]);
  not not_2 (not_2_out, Op[4]);
  not not_3 (not_3_out, Op[5]);
  not not_4 (not_4_out, Op[0]);
  not not_5 (not_5_out, Op[1]);
  not not_6 (not_6_out, Op[2]);
  and addu (addu_out, not_3_out, not_2_out, not_1_out, not_6_out, not_5_out, not_4_out);
  and subu (subu_out, not_3_out, not_2_out, not_1_out, not_6_out, not_5_out, not_4_out);
  and lw (lw_out, Op[5], not_2_out, not_1_out, not_6_out, Op[1], Op[0]);
  and sw (sw_out, Op[5], not_2_out, Op[3], not_6_out, Op[1], Op[0]);
  and beq (beq_out, not_3_out, not_2_out, not_1_out, Op[2], not_5_out, not_4_out);
  and lui (lui_out, not_3_out, not_2_out, Op[3], Op[2], Op[1], Op[0]);
  and ori (ExtOp, not_3_out, not_2_out, Op[3], Op[2], not_5_out, Op[0]);
  and ori_2 (temp, not_3_out, not_2_out, not_1_out, not_6_out, Op[1], Op[0]);
  or or_1 (RegDst, addu_out, subu_out);
  buf or_2 (branch, beq_out);  // OR_Gate
  buf or_3 (MemtoReg[1], lui_out);  // OR_Gate
  buf or_4 (MemRead, lw_out);  // OR_Gate
  buf or_5 (MemtoReg[0], lw_out);  // OR_Gate
  buf or_6 (MemWrite, sw_out);  // OR_Gate
  or or_7 (ALUOp[1], ExtOp, lui_out, beq_out);
  buf or_8 (ALUOp[2], lui_out);  // OR_Gate
  or or_9 (ALUOp[0], sw_out, lw_out, lui_out, ExtOp);
  or or_10 (ALUSrc, lw_out, sw_out, ExtOp);
  or or_11 (RegWrite, subu_out, addu_out, lw_out, lui_out, ExtOp, temp);
endmodule

module \GRF备用  (
  input  clk,
  input  reset,
  input  WE,
  input  [4:0] A1,
  input  [4:0] A2,
  input  [4:0] A3,
  input  [31:0] WD,
  output [31:0] RD1,
  output [31:0] RD2
);

  wire and_1_out, and_2_out, and_3_out, and_4_out, and_5_out, and_6_out, and_7_out, and_8_out, and_9_out,
       and_10_out, and_11_out, and_12_out, and_13_out, and_14_out, and_15_out, and_16_out, and_17_out,
       and_18_out, and_19_out, and_20_out, and_21_out, and_22_out, and_23_out, and_24_out, and_25_out,
       and_26_out, and_27_out, and_28_out, and_29_out, and_30_out, and_31_out, and_32_out, En0, En1, En2,
       En3, En4, En5, En6, En7, En8, En9, En10, En11, En12, En13, En14, En15, En16, En17, En18, En19, En20,
       En21, En22, En23, En24, En25, En26, En27, En28, En29, En30, En31, undriven_2, undriven_3;
  wire [31:0] NPC, out0, out1, out2, out3, out4, out5, out6, out7, out8, out9, out10, out11, out12, out13,
       out14, out15, out16, out17, out18, out19, out20, out21, out22, out23, out24, out25, out26, out27,
       out28, out29, out30, out31, pc_q, undriven;

  Demultiplexer #(.select(5), .enable("false")) demultiplexer_1 (
    .out0(En0), .out1(En1), .out2(En2), .out3(En3), .out4(En4), .out5(En5), .out6(En6), .out7(En7),
    .out8(En8), .out9(En9), .out10(En10), .out11(En11), .out12(En12), .out13(En13), .out14(En14),
    .out15(En15), .out16(En16), .out17(En17), .out18(En18), .out19(En19), .out20(En20), .out21(En21),
    .out22(En22), .out23(En23), .out24(En24), .out25(En25), .out26(En26), .out27(En27), .out28(En28),
    .out29(En29), .out30(En30), .out31(En31), .in(1'b1), .sel(A3));
  Register #(.width(32)) pc (.D(NPC), .en(1'b1), .Q(pc_q));  // open: clk, clr
  NPC npc_1 (.pc(pc_q), .imm(undriven), .zero(undriven_2), .branch(undriven_3));  // open: pc4, npc
  Multiplexer #(.select(5), .width(32)) multiplexer_1 (
    .in0(out0), .in1(out1), .in2(out2), .in3(out3), .in4(out4), .in5(out5), .in6(out6), .in7(out7),
    .in8(out8), .in9(out9), .in10(out10), .in11(out11), .in12(out12), .in13(out13), .in14(out14),
    .in15(out15), .in16(out16), .in17(out17), .in18(out18), .in19(out19), .in20(out20), .in21(out21),
    .in22(out22), .in23(out23), .in24(out24), .in25(out25), .in26(out26), .in27(out27), .in28(out28),
    .in29(out29), .in30(out30), .in31(out31), .out(RD2), .sel(A2), .en(1'b1));
  Multiplexer #(.select(5), .width(32)) multiplexer_2 (
    .in0(out0), .in1(out1), .in2(out2), .in3(out3), .in4(out4), .in5(out5), .in6(out6), .in7(out7),
    .in8(out8), .in9(out9), .in10(out10), .in11(out11), .in12(out12), .in13(out13), .in14(out14),
    .in15(out15), .in16(out16), .in17(out17), .in18(out18), .in19(out19), .in20(out20), .in21(out21),
    .in22(out22), .in23(out23), .in24(out24), .in25(out25), .in26(out26), .in27(out27), .in28(out28),
    .in29(out29), .in30(out30), .in31(out31), .out(RD1), .sel(A1), .en(1'b1));
  Register #(.width(32)) register_1 (.D({32{1'b0}}), .en(and_1_out), .Q(out0), .clk(clk), .clr(reset));
  and and_1 (and_1_out, En0, WE);
  Register #(.width(32)) register_2 (.D(WD), .en(and_2_out), .Q(out1), .clk(clk), .clr(reset));
  and and_2 (and_2_out, En1, WE);
  Register #(.width(32)) register_3 (.D(WD), .en(and_3_out), .Q(out5), .clk(clk), .clr(reset));
  and and_3 (and_3_out, En5, WE);
  Register #(.width(32)) register_4 (.D(WD), .en(and_4_out), .Q(out9), .clk(clk), .clr(reset));
  and and_4 (and_4_out, En9, WE);
  Register #(.width(32)) register_5 (.D(WD), .en(and_5_out), .Q(out13), .clk(clk), .clr(reset));
  and and_5 (and_5_out, En13, WE);
  Register #(.width(32)) register_6 (.D(WD), .en(and_6_out), .Q(out17), .clk(clk), .clr(reset));
  and and_6 (and_6_out, En17, WE);
  Register #(.width(32)) register_7 (.D(WD), .en(and_7_out), .Q(out21), .clk(clk), .clr(reset));
  and and_7 (and_7_out, En21, WE);
  Register #(.width(32)) register_8 (.D(WD), .en(and_8_out), .Q(out25), .clk(clk), .clr(reset));
  and and_8 (and_8_out, En25, WE);
  and and_9 (and_9_out, En29, WE);
  Register #(.width(32)) register_9 (.D(WD), .en(and_9_out), .Q(out29), .clk(clk), .clr(reset));
  and and_10 (and_10_out, En2, WE);
  and and_11 (and_11_out, En6, WE);
  and and_12 (and_12_out, En10, WE);
  and and_13 (and_13_out, En14, WE);
  and and_14 (and_14_out, En18, WE);
  and and_15 (and_15_out, En22, WE);
  and and_16 (and_16_out, En26, WE);
  Register #(.width(32)) register_10 (.D(WD), .en(and_10_out), .Q(out2), .clk(clk), .clr(reset));
  Register #(.width(32)) register_11 (.D(WD), .en(and_11_out), .Q(out6), .clk(clk), .clr(reset));
  Register #(.width(32)) register_12 (.D(WD), .en(and_12_out), .Q(out10), .clk(clk), .clr(reset));
  Register #(.width(32)) register_13 (.D(WD), .en(and_13_out), .Q(out14), .clk(clk), .clr(reset));
  Register #(.width(32)) register_14 (.D(WD), .en(and_14_out), .Q(out18), .clk(clk), .clr(reset));
  Register #(.width(32)) register_15 (.D(WD), .en(and_15_out), .Q(out22), .clk(clk), .clr(reset));
  Register #(.width(32)) register_16 (.D(WD), .en(and_16_out), .Q(out26), .clk(clk), .clr(reset));
  Register #(.width(32)) register_17 (.D(WD), .en(and_17_out), .Q(out30), .clk(clk), .clr(reset));
  and and_17 (and_17_out, En30, WE);
  Register #(.width(32)) register_18 (.D(WD), .en(and_18_out), .Q(out3), .clk(clk), .clr(reset));
  and and_18 (and_18_out, En3, WE);
  Register #(.width(32)) register_19 (.D(WD), .en(and_19_out), .Q(out7), .clk(clk), .clr(reset));
  and and_19 (and_19_out, En7, WE);
  Register #(.width(32)) register_20 (.D(WD), .en(and_20_out), .Q(out11), .clk(clk), .clr(reset));
  and and_20 (and_20_out, En11, WE);
  Register #(.width(32)) register_21 (.D(WD), .en(and_21_out), .Q(out15), .clk(clk), .clr(reset));
  and and_21 (and_21_out, En15, WE);
  Register #(.width(32)) register_22 (.D(WD), .en(and_22_out), .Q(out19), .clk(clk), .clr(reset));
  and and_22 (and_22_out, En19, WE);
  Register #(.width(32)) register_23 (.D(WD), .en(and_23_out), .Q(out23), .clk(clk), .clr(reset));
  and and_23 (and_23_out, En23, WE);
  Register #(.width(32)) register_24 (.D(WD), .en(and_24_out), .Q(out27), .clk(clk), .clr(reset));
  and and_24 (and_24_out, En27, WE);
  and and_25 (and_25_out, En31, WE);
  Register #(.width(32)) register_25 (.D(WD), .en(and_25_out), .Q(out31), .clk(clk), .clr(reset));
  and and_26 (and_26_out, En4, WE);
  and and_27 (and_27_out, En8, WE);
  and and_28 (and_28_out, En12, WE);
  and and_29 (and_29_out, En16, WE);
  and and_30 (and_30_out, En20, WE);
  and and_31 (and_31_out, En24, WE);
  and and_32 (and_32_out, En28, WE);
  Register #(.width(32)) register_26 (.D(WD), .en(and_26_out), .Q(out4), .clk(clk), .clr(reset));
  Register #(.width(32)) register_27 (.D(WD), .en(and_27_out), .Q(out8), .clk(clk), .clr(reset));
  Register #(.width(32)) register_28 (.D(WD), .en(and_28_out), .Q(out12), .clk(clk), .clr(reset));
  Register #(.width(32)) register_29 (.D(WD), .en(and_29_out), .Q(out16), .clk(clk), .clr(reset));
  Register #(.width(32)) register_30 (.D(WD), .en(and_30_out), .Q(out20), .clk(clk), .clr(reset));
  Register #(.width(32)) register_31 (.D(WD), .en(and_31_out), .Q(out24), .clk(clk), .clr(reset));
  Register #(.width(32)) register_32 (.D(WD), .en(and_32_out), .Q(out28), .clk(clk), .clr(reset));

  // Other names for the same wires on the sheet: RE = reset; WR = WE
endmodule

module IFU (
  input  clk,
  input  in_2,
  input  resset,
  input  [31:0] in_4,
  input  [27:0] in_5,
  input  zero,
  input  branch,
  output [31:0] pc4,
  output [31:0] instr
);

  wire and_1_out;
  wire [31:0] adder_2_out, multiplexer_1_out, NPC, pc_q;

  Register #(.width(32)) pc (.D(NPC), .en(1'b1), .Q(pc_q), .clk(clk), .clr(resset));
  Adder #(.width(32)) adder_1 (.a(32'h4), .b(pc_q), .out(pc4));  // open: cin, cout
  IM im_1 (.A(pc_q[6:2]), .Instr(instr));
  Adder #(.width(32)) adder_2 (.a(pc4), .b(in_4), .out(adder_2_out));  // open: cin, cout
  and and_1 (and_1_out, zero, branch);
  Multiplexer #(.width(32)) multiplexer_1 (
    .in0(pc4), .in1(adder_2_out), .out(multiplexer_1_out), .sel(and_1_out));  // open: en
  Multiplexer #(.width(32)) multiplexer_2 (
    .in0(multiplexer_1_out), .in1({pc_q[31:28], in_5}), .out(NPC), .sel(in_2));  // open: en
endmodule
