// Logisim project 对拍.circ as structural Verilog: 1 circuit, main circuit main
module main (
);

  wire and_1_out, comparator_1_eq, comparator_2_eq, comparator_3_eq, comparator_4_eq, comparator_5_eq,
       comparator_6_eq, comparator_7_eq, main_1_out_3, main_1_out_6, main_2_p3, main_2_p6;
  wire [4:0] main_1_out_4, main_1_out_7, main_2_p4, main_2_p7;
  wire [31:0] main_1_out_2, main_1_out_5, main_1_out_8, main_2_p2, main_2_p5, main_2_p8;

  Clock clock_1 ();  // open: out
  // Probe on main_2_p4
  cpu_0_2_main main_1 (
    .reset(1'b0), .out_2(main_1_out_2), .out_3(main_1_out_3), .out_4(main_1_out_4), .out_5(main_1_out_5),
    .out_6(main_1_out_6), .out_7(main_1_out_7), .out_8(main_1_out_8));
  // CPU3_02_main main_2: pin names not known; wires that end beside it: 1'b0, main_2_p2, main_2_p3, main_2_p4, main_2_p5, main_2_p6, main_2_p7, main_2_p8
  Comparator #(.width(1)) comparator_1 (.a(main_1_out_3), .b(main_2_p3), .eq(comparator_1_eq));  // open: gt, lt
  Comparator #(.width(32)) comparator_2 (.a(main_1_out_2), .b(main_2_p2), .eq(comparator_2_eq));  // open: gt, lt
  Comparator #(.width(5)) comparator_3 (.a(main_1_out_4), .b(main_2_p4), .eq(comparator_3_eq));  // open: gt, lt
  Comparator #(.width(32)) comparator_4 (.a(main_1_out_5), .b(main_2_p5), .eq(comparator_4_eq));  // open: gt, lt
  Comparator #(.width(1)) comparator_5 (.a(main_1_out_6), .b(main_2_p6), .eq(comparator_5_eq));  // open: gt, lt
  Comparator #(.width(5)) comparator_6 (.a(main_1_out_7), .b(main_2_p7), .eq(comparator_6_eq));  // open: gt, lt
  Comparator #(.width(32)) comparator_7 (.a(main_1_out_8), .b(main_2_p8), .eq(comparator_7_eq));  // open: gt, lt
  and and_1 (and_1_out, comparator_1_eq, comparator_2_eq, comparator_3_eq, comparator_4_eq, comparator_7_eq, comparator_5_eq);
  LED led_1 (.in(and_1_out));
endmodule
