// Logisim project 课下1CRC.circ as structural Verilog
module CRC (
  input  [7:0] A,
  input  [3:0] B,
  output [10:0] C
);

  wire n4bitsmod2_4_d;
  wire [2:0] n4bitsmod2_1_c, n4bitsmod2_2_c, n4bitsmod2_3_c, n4bitsmod2_4_c, n4bitsmod2_5_c, n4bitsmod2_6_c,
       n4bitsmod2_7_c;

  _4bitsmod2 u_4bitsmod2_1 (.A(A[7:4]), .B(B), .C(n4bitsmod2_1_c));  // open: D
  _4bitsmod2 u_4bitsmod2_2 (.A({n4bitsmod2_1_c, A[3]}), .B(B), .C(n4bitsmod2_2_c));  // open: D
  _4bitsmod2 u_4bitsmod2_3 (.A({n4bitsmod2_2_c, A[2]}), .B(B), .C(n4bitsmod2_3_c));  // open: D
  _4bitsmod2 u_4bitsmod2_4 (.A({n4bitsmod2_3_c, A[1]}), .B(B), .C(n4bitsmod2_4_c), .D(n4bitsmod2_4_d));
  _4bitsmod2 u_4bitsmod2_5 (.A({n4bitsmod2_4_c, A[0]}), .B(B), .C(n4bitsmod2_5_c));  // open: D
  _4bitsmod2 u_4bitsmod2_6 (.A({n4bitsmod2_5_c, 1'b0}), .B(B), .C(n4bitsmod2_6_c));  // open: D
  _4bitsmod2 u_4bitsmod2_7 (.A({n4bitsmod2_6_c, 1'b0}), .B(B), .C(n4bitsmod2_7_c));  // open: D
  _4bitsmod2 u_4bitsmod2_8 (.A({n4bitsmod2_7_c, 1'b0}), .B(B), .C(C[2:0]));  // open: D

  assign C[10:3] = A;
endmodule

module _4bitsmod2 (
  input  [3:0] A,
  input  [3:0] B,
  output [2:0] C,
  output D
);

  wire [2:0] xor_1_out;

  assign xor_1_out = A[2:0] ^ B[2:0];  // XOR_Gate xor_1, 3 bits wide
  Multiplexer #(.width(3)) multiplexer_1 (.in0(A[2:0]), .in1(xor_1_out), .out(C), .sel(A[3]));  // open: en

  assign D = A[3];

  // Other names for the same wires on the sheet: mux = A[3]
endmodule
