// Logisim project 课下2alu.circ as structural Verilog
module alu (
  input  [3:0] A,
  input  [3:0] B,
  input  [1:0] ALUOp,
  output [3:0] C
);

  wire [3:0] add, \and , \or , subi;

  Adder #(.width(4)) adder_1 (.a(A), .b(B), .out(add));  // open: cin, cout
  Subtractor #(.width(4)) subtractor_1 (.a(A), .b(B), .out(subi));  // open: bin, bout
  assign \and  = A & B;  // AND_Gate and_1, 4 bits wide
  assign \or  = A | B;  // OR_Gate or_1, 4 bits wide
  Multiplexer #(.select(2), .width(4)) multiplexer_1 (
    .in0(add), .in1(subi), .in2(\and ), .in3(\or ), .out(C), .sel(ALUOp));  // open: en

  // Other names for the same wires on the sheet: sel[1:0] = ALUOp
endmodule
