// Logisim project swap.circ as structural Verilog
module swap (
  input  l1,
  input  l2,
  input  S,
  output O1,
  output O2
);

  wire not_1_out, or_1_out, or_2_out, or_3_out, or_4_out;

  not not_1 (not_1_out, S);
  or or_1 (or_1_out, l1, S);
  or or_2 (or_2_out, l2, not_1_out);
  or or_3 (or_3_out, l1, not_1_out);
  or or_4 (or_4_out, l2, S);
  and and_1 (O1, or_1_out, or_2_out);
  and and_2 (O2, or_3_out, or_4_out);
endmodule
