// Logisim project 斐波拉子数列.circ as structural Verilog: 2 circuits, main circuit main
module main (
  input  [2:0] in,
  output [3:0] out
);

  wire clock_1_out, clock_2_out, clock_3_out, clock_4_out, comparator_1_eq, flag, not_2_out, register_1_q;
  wire [2:0] counter_1_q;
  wire [3:0] adder_1_out, multiplexer_1_out, register_2_q, register_3_q;

  Register #(.width(1)) register_1 (.D(1'b1), .en(flag), .Q(register_1_q), .clk(clock_1_out), .clr(1'b0));
  Clock clock_1 (.out(clock_1_out));
  Clock clock_2 (.out(clock_2_out));
  Counter #(.width(3), .max('h7)) counter_1 (
    .count(flag), .Q(counter_1_q), .clk(clock_2_out));  // open: load, D, carry, clr
  Multiplexer #(.width(4)) multiplexer_1 (
    .in0(4'b0001), .in1(register_2_q), .out(multiplexer_1_out), .sel(register_1_q));  // open: en
  Comparator #(.width(3)) comparator_1 (.a(counter_1_q), .b(in), .eq(comparator_1_eq));  // open: gt, lt
  not not_1 (flag, comparator_1_eq);
  Adder #(.width(4)) adder_1 (.a(multiplexer_1_out), .b(register_3_q), .out(adder_1_out));  // open: cin, cout
  Clock clock_3 (.out(clock_3_out));
  Register #(.width(4)) register_2 (.D(adder_1_out), .en(flag), .Q(register_2_q), .clk(clock_3_out), .clr(1'b0));
  Multiplexer #(.width(4)) multiplexer_2 (.in0(4'b0000), .in1(register_2_q), .out(out), .sel(not_2_out));  // open: en
  not not_2 (not_2_out, flag);
  Register #(.width(4)) register_3 (.D(register_2_q), .en(flag), .Q(register_3_q), .clk(clock_4_out));  // open: clr
  Clock clock_4 (.out(clock_4_out));
endmodule

module Main (
  input  in_1,
  input  [2:0] in_2,
  output [3:0] out_3
);

  wire clock_1_out, clock_2_out, comparator_1_eq;
  wire [2:0] adder_1_out, register_2_q;
  wire [2:1] undriven;
  wire [3:0] main_1_out;

  main main_1 (.in({undriven, in_1}), .out(main_1_out));
  Clock clock_1 (.out(clock_1_out));
  Clock clock_2 (.out(clock_2_out));
  Register #(.width(4)) register_1 (.D(main_1_out), .en(comparator_1_eq), .Q(out_3), .clk(clock_1_out), .clr(in_1));
  Adder #(.width(3)) adder_1 (.a(3'b001), .b(register_2_q), .out(adder_1_out));  // open: cin, cout
  Register #(.width(3)) register_2 (.D(adder_1_out), .en(1'b1), .Q(register_2_q), .clk(clock_2_out), .clr(in_1));
  Comparator #(.width(3)) comparator_1 (.a(register_2_q), .b(in_2), .eq(comparator_1_eq));  // open: gt, lt
  // Pins of 1 and 3 bits meet at {undriven, in_1}
endmodule
